# Fritzing sketch arduino_schematic_button (saved by Fritzing 0.9.4)
breadboards: 1

parts:
  Part2 = Arduino Uno (Rev3) - ICSP
  S3 = Pushbutton [package="[THT]"]

nets:
  N1: Part2.GND, S3.Pin_1, S3.Pin_2
  N2: Part2.D6_PWM, S3.Pin_3, S3.Pin_4
